// Logisim project cpu.circ as structural Verilog: 5 circuits, main circuit main
module main (
  input  [15:0] From_Instr_Mem,
  input  clk,
  output [15:0] r0,
  output [15:0] r1,
  output [15:0] r2,
  output [15:0] r3,
  output [15:0] Display_0,
  output [15:0] Display_1,
  output [15:0] To_Instr_Mem,
  output [15:0] Data_Mem_Data,
  output [15:0] Data_Mem_Addr,
  output Data_Mem_Write
);

  wire ALU_signed_overflow, ALUSrc, ExtOp, MemtoReg, not_1_out, nPC, RegDst, RegWr;
  wire [1:0] multiplexer_2_out;
  wire [3:0] ALUCtr;
  wire [5:0] funct;
  wire [7:6] imm;
  wire [15:0] ALUOut, ExtImm, multiplexer_1_out, multiplexer_3_out, pc, pc1, RdR1, RdR2, shifter_1_out,
       undriven, Write_Data;
  wire [15:8] instr;

  Hex_Digit_Display hex_digit_display_1 (.value(Display_0[15:12]));  // open: dp
  Hex_Digit_Display hex_digit_display_2 (.value(Display_0[11:8]));  // open: dp
  Hex_Digit_Display hex_digit_display_3 (.value(Display_0[3:0]));  // open: dp
  Hex_Digit_Display hex_digit_display_4 (.value(Display_0[7:4]));  // open: dp
  Shifter #(.width(16)) shifter_1 (.in(ExtImm), .\dist (4'b0010), .out(shifter_1_out));
  pipleline pipleline_1 (.iMem(From_Instr_Mem), .PC1(pc1), .iMem_Out({instr, imm, funct}), .PC_Out(pc), .clk(clk));
  Control control_1 (
    .opcode(instr[15:12]), .funct_code(funct), .RegWr(RegWr), .RegDst(RegDst), .ALUSrc(ExtOp),
    .ExtOp(ALUSrc), .nPC(nPC), .MemtoReg(MemtoReg), .MemWr(Data_Mem_Write), .ALUCtr(ALUCtr));
  Hex_Digit_Display hex_digit_display_5 (.value(Display_1[15:12]));  // open: dp
  Multiplexer #(.width(16), .enable("false")) multiplexer_1 (
    .in0(pc), .in1(undriven), .out(multiplexer_1_out), .sel(nPC));
  Adder #(.width(16)) adder_1 (.a(pc1), .b(shifter_1_out));  // open: out, cin, cout
  Multiplexer #(.width(2), .enable("false")) multiplexer_2 (
    .in0(instr[9:8]), .in1(imm), .out(multiplexer_2_out), .sel(RegDst));
  Hex_Digit_Display hex_digit_display_6 (.value(Display_1[7:4]));  // open: dp
  Hex_Digit_Display hex_digit_display_7 (.value(Display_1[11:8]));  // open: dp
  display u_display_1 (
    .opcode(instr[15:12]), .RdR1(RdR1), .RdR2(RdR2), .imm({imm, funct}), .display_1(Display_0),
    .display_2(Display_1), .clk(clk));
  Register #(.width(16)) register_1 (.D(multiplexer_1_out), .Q(To_Instr_Mem), .clk(clk));  // open: en, clr
  Hex_Digit_Display hex_digit_display_8 (.value(Display_1[3:0]));  // open: dp
  Adder #(.width(16)) adder_2 (.a(To_Instr_Mem), .b(16'h1), .out(pc1));  // open: cin, cout
  Regfile_main main (
    .Read_register_1(instr[11:10]), .Read_register_2(instr[9:8]), .write_register(multiplexer_2_out),
    .write_data(Write_Data), .Reg_0_Value(r0), .Reg_1_Value(r1), .Reg_2_Value(r2), .Reg_3_Value(r3),
    .RegWrite(RegWr), .clock(clk), .Read_Data_1(RdR1), .Read_Data_2(RdR2));
  assign Data_Mem_Addr = Data_Mem_Write ? ALUOut : 16'bz;  // Controlled_Buffer controlled_buffer_1
  Extender extender_1 (.Input({imm, funct}), .Result(ExtImm), .ExtOp(ExtOp));
  RAM #(.addrWidth(16), .dataWidth(16), .bus("separate")) ram_1 (
    .addr(Data_Mem_Addr), .din(RdR2), .data(Data_Mem_Data), .str(Data_Mem_Write), .sel(1'b1), .clk(clk),
    .ld(not_1_out), .clr(1'b0));
  not not_1 (not_1_out, Data_Mem_Write);
  Multiplexer #(.width(16), .enable("false")) multiplexer_3 (
    .in0(RdR2), .in1(ExtImm), .out(multiplexer_3_out), .sel(ALUSrc));
  LED OFlow (.in(ALU_signed_overflow));
  alu_main ALU (
    .switch__S(ALUCtr), .X(RdR1), .result(ALUOut), .signed_overflow(ALU_signed_overflow),
    .Y(multiplexer_3_out));  // open: equal
  Multiplexer #(.width(16), .enable("false")) multiplexer_4 (
    .in0(ALUOut), .in1(Data_Mem_Data), .out(Write_Data), .sel(MemtoReg));

  // Other names for the same wires on the sheet: d0[15:0] = Display_0; d1[15:0] = Display_1;
  //   from[15:0] = From_Instr_Mem; imm[5:0] = funct; instr[7:0] = {imm, funct}; rd[1:0] = imm; rt[1:0] = instr[9:8];
  //   rs[1:0] = instr[11:10]; opcode[3:0] = instr[15:12]; MemWr = Data_Mem_Write; pcOut[15:0] = To_Instr_Mem

  // Notes on the sheet:
  //   PC Out
  //   Decode
  //   PC Logic
  //   -LINING
  //   Branches & Jumps
  //   These are OUTPUTS to the circuit
  //   Registers
  //   PC+1 (eq PC+4)
  //   RAM
  //   Execute
  //   Memory
endmodule

module Control (
  input  [3:0] opcode,
  input  [5:0] funct_code,
  output RegWr,
  output RegDst,
  output ALUSrc,
  output ExtOp,
  output nPC,
  output MemtoReg,
  output MemWr,
  output [3:0] ALUCtr
);

  wire and_1_out, comparator_1_eq, comparator_2_eq, comparator_3_eq, comparator_4_eq, comparator_5_eq,
       comparator_6_eq, comparator_7_eq, comparator_8_lt, comparator_9_eq, not_1_out, or_1_out, or_2_out,
       or_3_out, or_4_out;
  wire [3:0] multiplexer_1_out;

  Comparator #(.width(4), .mode("unsigned")) comparator_1 (
    .a(opcode), .b(4'b1001), .eq(comparator_1_eq));  // open: gt, lt
  Comparator #(.width(4), .mode("unsigned")) comparator_2 (
    .a(opcode), .b(4'b1100), .eq(comparator_2_eq));  // open: gt, lt
  or or_1 (or_1_out, comparator_1_eq, comparator_2_eq);
  Comparator #(.width(4), .mode("unsigned")) comparator_3 (
    .a(opcode), .b(4'b0110), .eq(comparator_3_eq));  // open: gt, lt
  Comparator #(.width(4), .mode("unsigned")) comparator_4 (
    .a(opcode), .b(4'b0111), .eq(comparator_4_eq));  // open: gt, lt
  Comparator #(.width(4), .mode("unsigned")) comparator_5 (
    .a(opcode), .b(4'b1010), .eq(comparator_5_eq));  // open: gt, lt
  Comparator #(.width(4), .mode("unsigned")) comparator_6 (
    .a(opcode), .b(4'b1100), .eq(comparator_6_eq));  // open: gt, lt
  not not_1 (not_1_out, comparator_7_eq);
  Comparator #(.width(4), .mode("unsigned")) comparator_7 (
    .a(opcode), .b(4'b0000), .eq(comparator_7_eq));  // open: gt, lt
  Comparator #(.width(4), .mode("unsigned")) comparator_8 (
    .a(opcode), .b(4'b0101), .lt(comparator_8_lt));  // open: gt, eq
  nor nor_1 (RegWr, nPC, or_1_out);
  or or_2 (or_2_out, comparator_3_eq, comparator_4_eq);
  or or_3 (or_3_out, comparator_5_eq, comparator_6_eq);
  and and_1 (and_1_out, not_1_out, comparator_8_lt);
  Comparator #(.width(4), .mode("unsigned")) comparator_9 (
    .a(opcode), .b(4'b1000), .eq(comparator_9_eq));  // open: gt, lt
  not not_2 (ExtOp, or_4_out);
  or or_4 (or_4_out, or_2_out, or_3_out);
  or or_5 (nPC, and_1_out, comparator_9_eq);
  Multiplexer #(.select(4), .width(4), .enable("false")) multiplexer_1 (
    .in0(4'b0000), .in1(4'b0000), .in2(4'b0000), .in3(4'b0000), .in4(4'b0001), .in5(4'b0000), .in6(4'b0111),
    .in7(4'b0110), .in8(4'b0001), .in9(4'b0000), .in10(4'b0010), .in11(4'b0000), .in12(4'b0000),
    .in13(4'b0000), .in14(4'b0000), .in15(4'b0000), .out(multiplexer_1_out), .sel(opcode));
  or or_6 (ALUSrc, opcode[0], opcode[1], opcode[2], opcode[3]);
  Multiplexer #(.width(4), .enable("false")) multiplexer_2 (
    .in0(funct_code[3:0]), .in1(multiplexer_1_out), .out(ALUCtr), .sel(ALUSrc));
  Comparator #(.width(4), .mode("unsigned")) comparator_10 (.a(opcode), .b(4'b1011), .eq(MemtoReg));  // open: gt, lt
  Comparator #(.width(4), .mode("unsigned")) comparator_11 (.a(opcode), .b(4'b1001), .eq(MemWr));  // open: gt, lt

  assign RegDst = ALUSrc;

  // Other names for the same wires on the sheet: funct[5:0] = funct_code; op1 = ALUSrc; skip_instr = nPC

  // Notes on the sheet:
  //   Opcode or funct in ALU?
endmodule

// Ext?
module Extender (
  input  [7:0] Input,
  input  ExtOp,
  output [15:0] Result
);

  wire [15:0] bit_extender_1_out, bit_extender_2_out;

  assign bit_extender_1_out = {{8{1'b0}}, Input};  // Bit_Extender bit_extender_1
  Multiplexer #(.width(16), .enable("false")) multiplexer_1 (
    .in0(bit_extender_1_out), .in1(bit_extender_2_out), .out(Result), .sel(ExtOp));
  assign bit_extender_2_out = {{8{Input[7]}}, Input};  // Bit_Extender bit_extender_2

  // Notes on the sheet:
  //   Immediate
endmodule

module pipleline (
  input  [15:0] iMem,
  input  [15:0] PC1,
  input  clk,
  output [15:0] iMem_Out,
  output [15:0] PC_Out
);

  Register #(.width(16)) register_1 (.D(iMem), .Q(iMem_Out), .clk(clk));  // open: en, clr
  Register #(.width(16)) register_2 (.D(PC1), .Q(PC_Out), .clk(clk));  // open: en, clr
endmodule

module display (
  input  [3:0] opcode,
  input  [15:0] RdR1,
  input  [15:0] RdR2,
  input  [7:0] imm,
  input  clk,
  output [15:0] display_1,
  output [15:0] display_2
);

  wire and_1_out, and_2_out, comparator_1_eq, comparator_2_eq, comparator_3_eq;

  Comparator #(.width(4)) comparator_1 (.a(opcode), .b(4'b0000), .eq(comparator_1_eq));  // open: gt, lt
  Comparator comparator_2 (.a({8{1'b0}}), .b(imm), .eq(comparator_2_eq));  // open: gt, lt
  Register #(.width(16)) register_1 (.D(RdR1), .en(and_1_out), .Q(display_1), .clk(clk));  // open: clr
  and and_1 (and_1_out, comparator_1_eq, comparator_2_eq);
  and and_2 (and_2_out, comparator_1_eq, comparator_3_eq);
  Comparator comparator_3 (.a(8'h1), .b(imm), .eq(comparator_3_eq));  // open: gt, lt
  Register #(.width(16)) register_2 (.D(RdR2), .en(and_2_out), .Q(display_2), .clk(clk));  // open: clr

  // Other names for the same wires on the sheet: d0[15:0] = display_1; d1[15:0] = display_2
endmodule
